// Logisim project Aula Parte3_Hardware.circ as structural Verilog: 1 circuit, main circuit main
module main (
  input  REG_DESTINO,
  input  MEM_TO_REG,
  input  Alu_src,
  input  [3:0] in_4,
  input  \HABILITA_GRAVAÇÃO ,
  output [31:0] DADO_A_SER_GRAVADO,
  output [4:0] ORIGEM_2,
  output [4:0] REGISTRADOR_A_SER_GRAVADO,
  output [4:0] ORIGEM_1
);

  wire clock_1_out, clock_2_out, mipsprogramrom_1_p2, registerfile_1_p7;
  wire [31:0] adder_1_out, bit_extender_1_out, mips_alu_1_p4, mips_ram_1_p3, mipsprogramrom_1_p4,
       multiplexer_2_out, register_1_q, registerfile_1_p8;

  Register #(.width(32)) register_1 (
    .D(adder_1_out), .Q(register_1_q), .clk(clock_1_out), .clr(clock_1_out));  // open: en
  Adder #(.width(32)) adder_1 (.a(register_1_q), .b(32'h4), .out(adder_1_out));  // open: cin, cout
  Clock clock_1 (.out(clock_1_out));
  // MIPSProgramROM mipsprogramrom_1: pin names not known; wires that end beside it: register_1_q, mipsprogramrom_1_p2, mipsprogramrom_1_p2, {mipsprogramrom_1_p4[31:26], ORIGEM_1, ORIGEM_2, mipsprogramrom_1_p4[15:0]}
  Multiplexer #(.width(5)) multiplexer_1 (
    .in0(mipsprogramrom_1_p4[15:11]), .in1(ORIGEM_2), .out(REGISTRADOR_A_SER_GRAVADO), .sel(REG_DESTINO));  // open: en
  Clock clock_2 (.out(clock_2_out));
  assign bit_extender_1_out = {{16{1'b0}}, mipsprogramrom_1_p4[15:0]};  // Bit_Extender bit_extender_1
  // RegisterFile registerfile_1: pin names not known; wires that end beside it: DADO_A_SER_GRAVADO, clock_2_out, \HABILITA_GRAVAÇÃO , REGISTRADOR_A_SER_GRAVADO, ORIGEM_1, ORIGEM_2, registerfile_1_p7, registerfile_1_p8
  Multiplexer #(.width(32)) multiplexer_2 (
    .in0(registerfile_1_p8), .in1(bit_extender_1_out), .out(multiplexer_2_out), .sel(Alu_src));  // open: en
  // Mips_ALU mips_alu_1: pin names not known; wires that end beside it: registerfile_1_p7, multiplexer_2_out, in_4, mips_alu_1_p4
  Multiplexer #(.width(32)) multiplexer_3 (
    .in0(mips_alu_1_p4), .in1(mips_ram_1_p3), .out(DADO_A_SER_GRAVADO), .sel(MEM_TO_REG));  // open: en
  // MIPS_RAM mips_ram_1: pin names not known; wires that end beside it: mips_alu_1_p4[19:0], registerfile_1_p8, mips_ram_1_p3

  // Notes on the sheet:
  //   Memoria de programa
  //   R
  //   I
endmodule
